# Fritzing sketch projekt (saved by Fritzing 1.0.4)
breadboards: 1

parts:
  Bauteil1 = Motor Driver 1A Dual TB6612FNG
  Bauteil4 = Adafruit APDS-9960 [part_number="Adafruit #3595"]
  A1 = Wemos S2 Mini [part_number="WeMos D1 Mini Lite"]
  Power_plug1 = Power plug
  S1 = Pushbutton [package="[THT]"]
  S2 = Pushbutton [package="[THT]"]

nets:
  GND: Bauteil1.GND, Bauteil4.GND, A1.Pin_18, Power_plug1.GND
  VCC: Bauteil1.VCC, Bauteil4.VIN, A1.Pin_17, Power_plug1.VCC, S1.Pin_1, S1.Pin_2, S2.Pin_3, S2.Pin_4
  N1: Bauteil1.BIN1, A1.Pin_15
  N2: Bauteil1.PWMB, A1.Pin_14
  N3: Bauteil4.SCL, A1.Pin_4
  N4: Bauteil4.SDA, A1.Pin_12
  N5: A1.Pin_31, S2.Pin_1, S2.Pin_2
  N6: A1.Pin_32, S1.Pin_3, S1.Pin_4

custom parts:
  Adafruit APDS-9960: The APDS9960 from Avago Technologies has an integrated IR LED and driver, along with four directional photodiodes that sense reflected IR energy from the LED. It's proximity detection feature allows it to measure the distance an object is from the front of the sensor (up to a few centimeters) with 8 bit resolution. Since there are four IR sensors, you can measure the changes in light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
  Wemos S2 Mini: A mini wifi board based on the ESP32-S2FN4R2.
