# Fritzing sketch rabbit-hutch (saved by Fritzing 0.9.6b)
circuit board: 8.46667cm x 5.64444cm
breadboards: 1

parts:
  U1 = ESP32S-HiLetgo [part_number=ESP32S-HiLetgo]
  Bauteil1 = Motor Driver 1A Dual TB6612FNG
  M1 = DC Motor
  Bauteil2 = Adafruit APDS-9960 [part_number="Adafruit #3595"]
  S1 = Pushbutton [package="[THT]"]
  Power_plug1 = Power plug
  S2 = Pushbutton [package="[THT]"]

nets (from the schematic view):
  VCC: U1.3.3, Bauteil1.VCC, Bauteil2.3.3V
  N1: U1.GPIO34, Bauteil1.STBY
  N2: U1.GPIO35, Bauteil1.PWMB
  N3: U1.GPIO32, Bauteil1.BIN2
  N4: U1.GPIO33, Bauteil1.BIN1
  GND: U1.GND, Bauteil1.GND, Bauteil2.GND, S1.Pin_1, S1.Pin_2, Power_plug1.GND, S2.Pin_1
  VIN: U1.VIN, Bauteil1.VM, Bauteil2.VIN, Power_plug1.VCC
  N5: U1.GPIO6, Bauteil2.SCL
  N6: U1.GPIO7, Bauteil2.SDA
  N7: U1.GPIO22, S2.Pin_3, S2.Pin_4
  N8: U1.GPIO23, S1.Pin_3, S1.Pin_4
  N9: Bauteil1.B01, M1.pin_1
  N10: Bauteil1.B02, M1.pin_2

custom parts:
  ESP32S-HiLetgo: HiLetgo ESP-WROOM-32 ESP32 ESP-32S Development Board 2.4GHz Dual-Mode WiFi + Bluetooth Dual Cores Microcontroller The ESP32 integrated with Antenna switches, RF Balun, power amplifiers, low-noise amplifiers, filters, and management modules, and the entire solution occupies the least area of PCB. 2.4 GHz Wi-Fi plus Bluetooth dual-mode chip, with TSMC Ultra-low power consumption 40nm technology,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
  Adafruit APDS-9960: The APDS9960 from Avago Technologies has an integrated IR LED and driver, along with four directional photodiodes that sense reflected IR energy from the LED. It's proximity detection feature allows it to measure the distance an object is from the front of the sensor (up to a few centimeters) with 8 bit resolution. Since there are four IR sensors, you can measure the changes in light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
